# Fritzing sketch schematic (saved by Fritzing 0.9.3b)
breadboards: 1

parts:
  Adafruit_HUZZAH_ESP8266_Breakout1 = Adafruit HUZZAH ESP8266 Breakout [part_number=2471]
  R1 = Resistor [tolerance=±5% resistance=220 package="0603 [SMD]"]
  R2 = Resistor [tolerance=±5% resistance=1M package="0603 [SMD]"]
  U1 = LIPO-1000mAh [package=lipo-1000]
  3-pins_Hall_Effect_Sensor1 = mystery part, 3 pins [chip_label="Hall Effect Sensor"]
  S1 = Toggle Switch [package=THT]

nets:
  N1: Adafruit_HUZZAH_ESP8266_Breakout1.GND, R1.Pin_1, 3-pins_Hall_Effect_Sensor1.pin3, S1.L2
  N2: Adafruit_HUZZAH_ESP8266_Breakout1.VBat, R2.Pin_1, U1.+
  N3: Adafruit_HUZZAH_ESP8266_Breakout1.A, R1.Pin_0, R2.Pin_0
  N4: Adafruit_HUZZAH_ESP8266_Breakout1.#2, 3-pins_Hall_Effect_Sensor1.pin2
  N5: Adafruit_HUZZAH_ESP8266_Breakout1.3V, 3-pins_Hall_Effect_Sensor1.pin1
  N6: U1.-, S1.L1
